// Logisim project 1801CS01_A3.circ as structural Verilog: 5 circuits, main circuit main
module main (
  input  CLR_L
);

  wire bcd_to_7_segmentdecoder_1_a_2, bcd_to_7_segmentdecoder_1_b_2, bcd_to_7_segmentdecoder_1_c_2,
       bcd_to_7_segmentdecoder_1_d_2, bcd_to_7_segmentdecoder_1_e, bcd_to_7_segmentdecoder_1_f,
       bcd_to_7_segmentdecoder_1_g, bcd_to_7_segmentdecoder_2_a_2, bcd_to_7_segmentdecoder_2_b_2,
       bcd_to_7_segmentdecoder_2_c_2, bcd_to_7_segmentdecoder_2_d_2, bcd_to_7_segmentdecoder_2_e,
       bcd_to_7_segmentdecoder_2_f, bcd_to_7_segmentdecoder_2_g, bcd_to_7_segmentdecoder_3_a_2,
       bcd_to_7_segmentdecoder_3_b_2, bcd_to_7_segmentdecoder_3_c_2, bcd_to_7_segmentdecoder_3_d_2,
       bcd_to_7_segmentdecoder_3_e, bcd_to_7_segmentdecoder_3_f, bcd_to_7_segmentdecoder_3_g,
       bcd_to_7_segmentdecoder_4_a_2, bcd_to_7_segmentdecoder_4_b_2, bcd_to_7_segmentdecoder_4_c_2,
       bcd_to_7_segmentdecoder_4_d_2, bcd_to_7_segmentdecoder_4_e, bcd_to_7_segmentdecoder_4_f,
       bcd_to_7_segmentdecoder_4_g, CLOCK_out, mod_6counter_1_q0, mod_6counter_1_q1, mod_6counter_1_q2,
       mod_6counter_1_z, mod_10counter_1_q0, mod_10counter_1_q1, mod_10counter_1_q2, mod_10counter_1_q3,
       mod_10counter_1_z, n12_hour_counter_1_a0, n12_hour_counter_1_b0, n12_hour_counter_1_b1,
       n12_hour_counter_1_b2, n12_hour_counter_1_b3;

  Clock CLOCK (.out(CLOCK_out));
  Mod_10Counter mod_10counter_1 (
    .CLK(CLOCK_out), .CLR(CLR_L), .q3(mod_10counter_1_q3), .q2(mod_10counter_1_q2), .q1(mod_10counter_1_q1),
    .q0(mod_10counter_1_q0), .Z(mod_10counter_1_z));
  Mod_6Counter mod_6counter_1 (
    .E(mod_10counter_1_z), .CLK(CLOCK_out), .CLR(CLR_L), .q2(mod_6counter_1_q2), .q1(mod_6counter_1_q1),
    .q0(mod_6counter_1_q0), .Z(mod_6counter_1_z));
  _12_Hour_Counter u_12_hour_counter_1 (
    .EN(mod_6counter_1_z), .CLK(CLOCK_out), .CLR(CLR_L), .A0(n12_hour_counter_1_a0),
    .B3(n12_hour_counter_1_b3), .B2(n12_hour_counter_1_b2), .B1(n12_hour_counter_1_b1),
    .B0(n12_hour_counter_1_b0));
  BCD_TO_7_SegmentDecoder bcd_to_7_segmentdecoder_1 (
    .A(mod_10counter_1_q3), .B(mod_10counter_1_q2), .C(mod_10counter_1_q1), .D(mod_10counter_1_q0),
    .a_2(bcd_to_7_segmentdecoder_1_a_2), .b_2(bcd_to_7_segmentdecoder_1_b_2),
    .c_2(bcd_to_7_segmentdecoder_1_c_2), .d_2(bcd_to_7_segmentdecoder_1_d_2),
    .e(bcd_to_7_segmentdecoder_1_e), .f(bcd_to_7_segmentdecoder_1_f), .g(bcd_to_7_segmentdecoder_1_g));
  BCD_TO_7_SegmentDecoder bcd_to_7_segmentdecoder_2 (
    .A(1'b0), .B(mod_6counter_1_q2), .C(mod_6counter_1_q1), .D(mod_6counter_1_q0),
    .a_2(bcd_to_7_segmentdecoder_2_a_2), .b_2(bcd_to_7_segmentdecoder_2_b_2),
    .c_2(bcd_to_7_segmentdecoder_2_c_2), .d_2(bcd_to_7_segmentdecoder_2_d_2),
    .e(bcd_to_7_segmentdecoder_2_e), .f(bcd_to_7_segmentdecoder_2_f), .g(bcd_to_7_segmentdecoder_2_g));
  BCD_TO_7_SegmentDecoder bcd_to_7_segmentdecoder_3 (
    .A(n12_hour_counter_1_b3), .B(n12_hour_counter_1_b2), .C(n12_hour_counter_1_b1),
    .D(n12_hour_counter_1_b0), .a_2(bcd_to_7_segmentdecoder_3_a_2), .b_2(bcd_to_7_segmentdecoder_3_b_2),
    .c_2(bcd_to_7_segmentdecoder_3_c_2), .d_2(bcd_to_7_segmentdecoder_3_d_2),
    .e(bcd_to_7_segmentdecoder_3_e), .f(bcd_to_7_segmentdecoder_3_f), .g(bcd_to_7_segmentdecoder_3_g));
  BCD_TO_7_SegmentDecoder bcd_to_7_segmentdecoder_4 (
    .A(1'b0), .B(1'b0), .C(1'b0), .D(n12_hour_counter_1_a0), .a_2(bcd_to_7_segmentdecoder_4_a_2),
    .b_2(bcd_to_7_segmentdecoder_4_b_2), .c_2(bcd_to_7_segmentdecoder_4_c_2),
    .d_2(bcd_to_7_segmentdecoder_4_d_2), .e(bcd_to_7_segmentdecoder_4_e), .f(bcd_to_7_segmentdecoder_4_f),
    .g(bcd_to_7_segmentdecoder_4_g));
  _7_Segment_Display u_7_segment_display_1 (
    .g(bcd_to_7_segmentdecoder_4_g), .f(bcd_to_7_segmentdecoder_4_f), .a(bcd_to_7_segmentdecoder_4_a_2),
    .b(bcd_to_7_segmentdecoder_4_b_2), .e(bcd_to_7_segmentdecoder_4_e), .d(bcd_to_7_segmentdecoder_4_d_2),
    .c(bcd_to_7_segmentdecoder_4_c_2));  // open: dp
  _7_Segment_Display u_7_segment_display_2 (
    .g(bcd_to_7_segmentdecoder_3_g), .f(bcd_to_7_segmentdecoder_3_f), .a(bcd_to_7_segmentdecoder_3_a_2),
    .b(bcd_to_7_segmentdecoder_3_b_2), .e(bcd_to_7_segmentdecoder_3_e), .d(bcd_to_7_segmentdecoder_3_d_2),
    .c(bcd_to_7_segmentdecoder_3_c_2));  // open: dp
  _7_Segment_Display u_7_segment_display_3 (
    .g(bcd_to_7_segmentdecoder_2_g), .f(bcd_to_7_segmentdecoder_2_f), .a(bcd_to_7_segmentdecoder_2_a_2),
    .b(bcd_to_7_segmentdecoder_2_b_2), .e(bcd_to_7_segmentdecoder_2_e), .d(bcd_to_7_segmentdecoder_2_d_2),
    .c(bcd_to_7_segmentdecoder_2_c_2));  // open: dp
  _7_Segment_Display u_7_segment_display_4 (
    .g(bcd_to_7_segmentdecoder_1_g), .f(bcd_to_7_segmentdecoder_1_f), .a(bcd_to_7_segmentdecoder_1_a_2),
    .b(bcd_to_7_segmentdecoder_1_b_2), .e(bcd_to_7_segmentdecoder_1_e), .d(bcd_to_7_segmentdecoder_1_d_2),
    .c(bcd_to_7_segmentdecoder_1_c_2));  // open: dp

  // Notes on the sheet:
  //   12-Hour Clock
endmodule

module BCD_TO_7_SegmentDecoder (
  input  A,
  input  B,
  input  C,
  input  D,
  output a_2,
  output b_2,
  output c_2,
  output d_2,
  output e,
  output f,
  output g
);

  wire B_prime_C_out, B_prime_D_prime_out, BC_prime_D_out, BC_prime_out, BD_out, BD_prime_out,
       C_prime_D_prime_out, CD_out, CD_prime_out, not_1_out, not_2_out, not_3_out;

  not not_1 (not_1_out, B);
  not not_2 (not_2_out, C);
  not not_3 (not_3_out, D);
  and BD (BD_out, B, D);
  and B_prime_D_prime (B_prime_D_prime_out, not_1_out, not_3_out);
  and C_prime_D_prime (C_prime_D_prime_out, not_2_out, not_3_out);
  and CD (CD_out, C, D);
  and CD_prime (CD_prime_out, not_3_out, C);
  and BC_prime_D (BC_prime_D_out, B, not_2_out, D);
  and B_prime_C (B_prime_C_out, not_1_out, C);
  and BC_prime (BC_prime_out, B, not_2_out);
  and BD_prime (BD_prime_out, B, not_3_out);
  or or_1 (a_2, A, C, BD_out, B_prime_D_prime_out);
  or or_2 (b_2, not_1_out, C_prime_D_prime_out, CD_out);
  or or_3 (c_2, B, not_2_out, D);
  or or_4 (d_2, B_prime_D_prime_out, CD_prime_out, BC_prime_D_out, B_prime_C_out, A);
  or or_5 (e, B_prime_D_prime_out, CD_prime_out);
  or or_6 (f, A, C_prime_D_prime_out, BC_prime_out, BD_prime_out);
  or or_7 (g, A, BC_prime_out, B_prime_C_out, CD_prime_out);
endmodule

module Mod_10Counter (
  input  CLK,
  input  CLR,
  output q3,
  output q2,
  output q1,
  output q0,
  output Z
);

  wire and_1_out, and_2_out, and_3_out, and_4_out, and_5_out, and_6_out, and_7_out, not_1_out, not_2_out,
       not_3_out, not_4_out, or_1_out, or_2_out, or_3_out;

  D_Flip_Flop d_ff_1 (.clk(CLK), .D(not_1_out), .Q(q0), .reset(CLR));  // open: Qn, preset, en
  not not_1 (not_1_out, q0);
  and and_1 (and_1_out, q0, not_2_out, not_4_out);
  or or_1 (or_1_out, and_1_out, and_2_out);
  and and_2 (and_2_out, q1, not_1_out);
  not not_2 (not_2_out, q1);
  D_Flip_Flop d_ff_2 (.clk(CLK), .D(or_1_out), .Q(q1), .reset(CLR));  // open: Qn, preset, en
  and and_3 (and_3_out, not_3_out, q0, q1);
  and and_4 (and_4_out, not_1_out, q2);
  and and_5 (and_5_out, q2, not_2_out);
  or or_2 (or_2_out, and_3_out, and_4_out, and_5_out);
  not not_3 (not_3_out, q2);
  D_Flip_Flop d_ff_3 (.clk(CLK), .D(or_2_out), .Q(q2), .reset(CLR));  // open: Qn, preset, en
  and and_6 (and_6_out, q0, q1, q2);
  and and_7 (and_7_out, not_1_out, q3);
  or or_3 (or_3_out, and_6_out, and_7_out);
  not not_4 (not_4_out, q3);
  D_Flip_Flop d_ff_4 (.clk(CLK), .D(or_3_out), .Q(q3), .reset(CLR));  // open: Qn, preset, en
  and and_8 (Z, q3, q0);

  // Notes on the sheet:
  //   Mod-10 Counter
endmodule

module Mod_6Counter (
  input  E,
  input  CLK,
  input  CLR,
  output q2,
  output q1,
  output q0,
  output Z
);

  wire and_1_out, and_2_out, and_3_out, and_4_out, and_5_out, and_6_out, not_1_out, not_2_out, not_3_out,
       not_4_out, not_5_out, or_1_out, or_2_out, xor_1_out;

  D_Flip_Flop d_ff_1 (.clk(CLK), .D(xor_1_out), .Q(q0), .reset(CLR));  // open: Qn, preset, en
  xor xor_1 (xor_1_out, q0, E);
  not not_1 (not_1_out, q0);
  not not_2 (not_2_out, E);
  and and_1 (and_1_out, E, q0, not_3_out, not_5_out);
  and and_2 (and_2_out, not_2_out, q1);
  and and_3 (and_3_out, q1, not_1_out);
  or or_1 (or_1_out, and_1_out, and_2_out, and_3_out);
  not not_3 (not_3_out, q1);
  not not_4 (not_4_out, E);
  D_Flip_Flop d_ff_2 (.clk(CLK), .D(or_1_out), .Q(q1), .reset(CLR));  // open: Qn, preset, en
  and and_4 (and_4_out, not_4_out, q2);
  and and_5 (and_5_out, not_1_out, q2);
  and and_6 (and_6_out, q1, q0, E);
  not not_5 (not_5_out, q2);
  or or_2 (or_2_out, and_4_out, and_5_out, and_6_out);
  D_Flip_Flop d_ff_3 (.clk(CLK), .D(or_2_out), .Q(q2), .reset(CLR));  // open: Qn, preset, en
  and and_7 (Z, q2, E, q0);

  // Notes on the sheet:
  //   Mod-6 Counter
endmodule

module _12_Hour_Counter (
  input  EN,
  input  CLK,
  input  CLR,
  output A0,
  output B3,
  output B2,
  output B1,
  output B0
);

  wire and_1_out, and_2_out, and_3_out, and_4_out, and_5_out, and_6_out, and_7_out, and_8_out, and_9_out,
       and_11_out, d_ff_2_q, d_ff_4_q, not_1_out, not_2_out, not_3_out, not_4_out, or_1_out, or_2_out,
       xor_1_out;

  D_Flip_Flop d_ff_1 (.clk(CLK), .D(not_1_out), .Q(B0), .en(EN), .reset(CLR));  // open: Qn, preset
  not not_1 (not_1_out, B0);
  xor xor_1 (xor_1_out, d_ff_2_q, B0);
  D_Flip_Flop d_ff_2 (.clk(CLK), .D(xor_1_out), .Q(d_ff_2_q), .en(EN), .reset(CLR));  // open: Qn, preset
  not not_2 (not_2_out, d_ff_2_q);
  and and_1 (and_1_out, d_ff_2_q, B0, not_4_out, not_3_out);
  and and_2 (and_2_out, not_1_out, B2);
  and and_3 (and_3_out, B2, not_2_out);
  or or_1 (or_1_out, and_1_out, and_2_out, and_3_out);
  not not_3 (not_3_out, B2);
  D_Flip_Flop d_ff_3 (.clk(CLK), .D(or_1_out), .Q(B2), .en(EN), .reset(CLR));  // open: Qn, preset
  and and_4 (and_4_out, B0, d_ff_2_q, B2);
  or or_2 (or_2_out, and_4_out, and_5_out, and_6_out);
  and and_5 (and_5_out, d_ff_4_q, not_2_out);
  and and_6 (and_6_out, d_ff_4_q, not_1_out);
  D_Flip_Flop d_ff_4 (.clk(CLK), .D(or_2_out), .Q(d_ff_4_q), .en(EN), .reset(CLR));  // open: Qn, preset
  not not_4 (not_4_out, d_ff_4_q);
  and and_7 (and_7_out, not_1_out, not_4_out, not_3_out);
  and and_8 (and_8_out, not_4_out, d_ff_2_q);
  and and_9 (and_9_out, not_4_out, not_3_out, not_2_out, not_1_out);
  or or_3 (B1, and_7_out, and_8_out);
  and and_10 (B3, d_ff_4_q, not_2_out);
  or or_4 (A0, and_9_out, and_11_out);
  and and_11 (and_11_out, d_ff_2_q, d_ff_4_q);

  // Notes on the sheet:
  //   12-Hour Counter
endmodule
