// Logisim project 1801SC01_A2.circ as structural Verilog: 1 circuit, main circuit main
module main (
  input  I0,
  input  I1,
  output Output
);

  wire and_1_out, and_2_out, and_3_out, and_4_out, and_5_out, and_6_out, clock_1_out, not_1_out, not_2_out,
       not_3_out, not_4_out, or_1_out, or_2_out, Q0_q, Q1_q;

  not not_1 (not_1_out, I0);
  Clock clock_1 (.out(clock_1_out));
  not not_2 (not_2_out, I1);
  and and_1 (and_1_out, I1, not_4_out, Q0_q);
  and and_2 (and_2_out, not_4_out, Q0_q, not_1_out);
  and and_3 (and_3_out, not_2_out, I0, Q1_q, not_3_out);
  D_Flip_Flop Q0 (.clk(clock_1_out), .D(or_1_out), .Q(Q0_q));  // open: Qn, preset, en, reset
  or or_1 (or_1_out, and_1_out, and_2_out, and_3_out);
  not not_3 (not_3_out, Q0_q);
  and and_4 (and_4_out, I1, I0, not_4_out, Q0_q);
  and and_5 (and_5_out, not_1_out, Q1_q, not_3_out);
  and and_6 (and_6_out, not_3_out, not_2_out, not_1_out);
  or or_2 (or_2_out, and_5_out, and_6_out, and_4_out);
  and and_7 (Output, Q0_q, Q1_q);
  D_Flip_Flop Q1 (.clk(clock_1_out), .D(or_2_out), .Q(Q1_q));  // open: Qn, preset, en, reset
  not not_4 (not_4_out, Q1_q);

  // Notes on the sheet:
  //   Finite State Machine Circuit Diagram
endmodule
